// Logisim project bumpCounter.circ as structural Verilog: 1 circuit, main circuit bumpCounter
module bumpCounter (
  input  [7:0] delayTime,
  input  start,
  input  clock,
  output \output 
);

  wire counter_1_carry, not_1_out, register_1_q;

  not not_1 (not_1_out, \output );
  Counter counter_1 (
    .load(start), .D(delayTime), .count(not_1_out), .carry(counter_1_carry), .clk(clock), .clr(register_1_q));  // open: Q
  Register #(.width(1)) register_1 (.D(counter_1_carry), .en(start), .Q(register_1_q), .clk(clock));  // open: clr
  Register #(.width(1)) register_2 (.D(register_1_q), .en(start), .Q(\output ), .clk(clock));  // open: clr
endmodule
