// Logisim project bumpIncoder32.circ as structural Verilog: 1 circuit, main circuit bumpIncoder32
module bumpIncoder32 (
  input  [31:0] start_data,
  input  start,
  input  clock,
  input  reset,
  output [31:0] display1,
  output [31:0] display3,
  output [31:0] display5,
  output [31:0] display7,
  output [31:0] display9,
  output [31:0] display11,
  output [31:0] display13,
  output [31:0] display15,
  output [31:0] display17,
  output [31:0] display19,
  output [31:0] display21,
  output [31:0] display23,
  output [31:0] display25,
  output [31:0] display27,
  output [31:0] display29,
  output [31:0] display31,
  output [31:0] display2,
  output [31:0] display4,
  output [31:0] display6,
  output [31:0] display8,
  output [31:0] display10,
  output [31:0] display12,
  output [31:0] display14,
  output [31:0] display16,
  output [31:0] display18,
  output [31:0] display20,
  output [31:0] display22,
  output [31:0] display24,
  output [31:0] display26,
  output [31:0] display28,
  output [31:0] display30,
  output [31:0] display32,
  output [31:0] final_data,
  output start_output,
  output clock_output,
  output reset_output
);

  Register #(.width(32)) register_1 (.D(start_data), .en(start), .Q(display1), .clk(clock), .clr(reset));
  Register #(.width(32)) register_2 (.D(display1), .en(start), .Q(display2), .clk(clock), .clr(reset));
  Register #(.width(32)) register_3 (.D(display2), .en(start), .Q(display3), .clk(clock), .clr(reset));
  Register #(.width(32)) register_4 (.D(display3), .en(start), .Q(display4), .clk(clock), .clr(reset));
  Register #(.width(32)) register_5 (.D(display4), .en(start), .Q(display5), .clk(clock), .clr(reset));
  Register #(.width(32)) register_6 (.D(display5), .en(start), .Q(display6), .clk(clock), .clr(reset));
  Register #(.width(32)) register_7 (.D(display7), .en(start), .Q(display8), .clk(clock), .clr(reset));
  Register #(.width(32)) register_8 (.D(display6), .en(start), .Q(display7), .clk(clock), .clr(reset));
  Register #(.width(32)) register_9 (.D(display8), .en(start), .Q(display9), .clk(clock), .clr(reset));
  Register #(.width(32)) register_10 (.D(display9), .en(start), .Q(display10), .clk(clock), .clr(reset));
  Register #(.width(32)) register_11 (.D(display10), .en(start), .Q(display11), .clk(clock), .clr(reset));
  Register #(.width(32)) register_12 (.D(display12), .en(start), .Q(display13), .clk(clock), .clr(reset));
  Register #(.width(32)) register_13 (.D(display11), .en(start), .Q(display12), .clk(clock), .clr(reset));
  Register #(.width(32)) register_14 (.D(display13), .en(start), .Q(display14), .clk(clock), .clr(reset));
  Register #(.width(32)) register_15 (.D(display15), .en(start), .Q(display16), .clk(clock), .clr(reset));
  Register #(.width(32)) register_16 (.D(display14), .en(start), .Q(display15), .clk(clock), .clr(reset));
  Register #(.width(32)) register_17 (.D(display16), .en(start), .Q(display17), .clk(clock), .clr(reset));
  Register #(.width(32)) register_18 (.D(display18), .en(start), .Q(display19), .clk(clock), .clr(reset));
  Register #(.width(32)) register_19 (.D(display17), .en(start), .Q(display18), .clk(clock), .clr(reset));
  Register #(.width(32)) register_20 (.D(display19), .en(start), .Q(display20), .clk(clock), .clr(reset));
  Register #(.width(32)) register_21 (.D(display20), .en(start), .Q(display21), .clk(clock), .clr(reset));
  Register #(.width(32)) register_22 (.D(display21), .en(start), .Q(display22), .clk(clock), .clr(reset));
  Register #(.width(32)) register_23 (.D(display23), .en(start), .Q(display24), .clk(clock), .clr(reset));
  Register #(.width(32)) register_24 (.D(display22), .en(start), .Q(display23), .clk(clock), .clr(reset));
  Register #(.width(32)) register_25 (.D(display24), .en(start), .Q(display25), .clk(clock), .clr(reset));
  Register #(.width(32)) register_26 (.D(display26), .en(start), .Q(display27), .clk(clock), .clr(reset));
  Register #(.width(32)) register_27 (.D(display25), .en(start), .Q(display26), .clk(clock), .clr(reset));
  Register #(.width(32)) register_28 (.D(display28), .en(start), .Q(display29), .clk(clock), .clr(reset));
  Register #(.width(32)) register_29 (.D(display27), .en(start), .Q(display28), .clk(clock), .clr(reset));
  Register #(.width(32)) register_30 (.D(display29), .en(start), .Q(display30), .clk(clock), .clr(reset));
  Register #(.width(32)) register_31 (.D(display30), .en(start), .Q(display31), .clk(clock), .clr(reset));
  Register #(.width(32)) register_32 (.D(display31), .en(start), .Q(display32), .clk(clock), .clr(reset));

  assign clock_output = clock;
  assign final_data = display32;
  assign reset_output = reset;
  assign start_output = start;
endmodule
