// Logisim project pushBump32.circ as structural Verilog: 1 circuit, main circuit pushBump32
module pushBump32 (
  input  [31:0] ground,
  input  [31:0] block1,
  input  [31:0] block2,
  input  [31:0] block3,
  input  [31:0] block4,
  input  start,
  input  clock,
  input  reset,
  input  making,
  output [31:0] \output 
);

  wire not_1_out;
  wire [31:0] controlled_buffer_1_out, controlled_buffer_3_out, controlled_buffer_5_out,
       controlled_buffer_7_out, or_1_out, or_2_out, or_3_out, or_4_out, register_1_q, register_2_q,
       register_3_q, register_4_q, register_5_q;

  not not_1 (not_1_out, making);
  assign or_1_out = ground | block1;  // OR_Gate or_1, 32 bits wide
  assign controlled_buffer_1_out = making ? or_1_out : 32'bz;  // Controlled_Buffer controlled_buffer_1
  Register #(.width(32)) register_1 (.D(ground), .en(start), .Q(register_1_q), .clk(clock), .clr(reset));
  assign controlled_buffer_1_out = not_1_out ? register_1_q : 32'bz;  // Controlled_Buffer controlled_buffer_2
  assign or_2_out = ground | block2;  // OR_Gate or_2, 32 bits wide
  assign controlled_buffer_3_out = making ? or_2_out : 32'bz;  // Controlled_Buffer controlled_buffer_3
  assign controlled_buffer_3_out = not_1_out ? register_2_q : 32'bz;  // Controlled_Buffer controlled_buffer_4
  Register #(.width(32)) register_2 (
    .D(controlled_buffer_1_out), .en(start), .Q(register_2_q), .clk(clock), .clr(reset));
  Register #(.width(32)) register_3 (
    .D(controlled_buffer_3_out), .en(start), .Q(register_3_q), .clk(clock), .clr(reset));
  assign or_3_out = ground | block3;  // OR_Gate or_3, 32 bits wide
  assign controlled_buffer_5_out = making ? or_3_out : 32'bz;  // Controlled_Buffer controlled_buffer_5
  assign controlled_buffer_5_out = not_1_out ? register_3_q : 32'bz;  // Controlled_Buffer controlled_buffer_6
  assign controlled_buffer_7_out = not_1_out ? register_4_q : 32'bz;  // Controlled_Buffer controlled_buffer_7
  Register #(.width(32)) register_4 (
    .D(controlled_buffer_5_out), .en(start), .Q(register_4_q), .clk(clock), .clr(reset));
  assign or_4_out = ground | block4;  // OR_Gate or_4, 32 bits wide
  assign controlled_buffer_7_out = making ? or_4_out : 32'bz;  // Controlled_Buffer controlled_buffer_8
  Register #(.width(32)) register_5 (
    .D(controlled_buffer_7_out), .en(start), .Q(register_5_q), .clk(clock), .clr(reset));
  Register #(.width(32)) register_6 (.D(register_5_q), .en(start), .Q(\output ), .clk(clock), .clr(reset));
endmodule
